// Logisim project control_logic.circ as structural Verilog: 1 circuit, main circuit control_logic
module control_logic (
  input  [31:0] inst,
  input  BrEq,
  input  BrLt,
  output PCSel,
  output RegWEn,
  output [2:0] ImmSel,
  output BrUn,
  output ASel,
  output BSel,
  output [3:0] ALUSel,
  output MemRW,
  output [1:0] WBSel,
  output CSRSel,
  output CSRWen
);

  wire and_6_out, and_7_out, and_8_out, and_9_out, and_10_out, and_11_out, and_12_out, comparator_1_eq,
       comparator_2_eq, comparator_3_eq, comparator_4_gt, comparator_5_eq, comparator_6_eq, comparator_7_eq,
       comparator_8_eq, comparator_9_eq, comparator_10_gt, comparator_11_eq, comparator_12_eq,
       comparator_13_eq, comparator_14_eq, comparator_15_eq, comparator_17_eq, comparator_18_eq,
       comparator_19_eq, comparator_20_eq, comparator_27_eq, comparator_28_eq, comparator_29_eq,
       comparator_30_eq, comparator_31_eq, comparator_32_eq, comparator_33_eq, comparator_34_eq,
       comparator_35_eq, comparator_36_eq, is_CSRWI, is_I_Type, is_JALR_Type, is_LOAD_Type, is_R_Type,
       is_SB_Type, is_U_Type, is_UJ_Type, isMUL, isMULh, isSRA, isSUB, not_1_out, not_2_out, not_3_out,
       or_1_out, or_4_out, or_6_out, or_9_out;
  wire [1:0] multiplexer_12_out;
  wire [2:0] multiplexer_8_out, multiplexer_9_out, multiplexer_10_out, multiplexer_11_out, multiplexer_13_out;
  wire [3:0] multiplexer_2_out, multiplexer_3_out, multiplexer_4_out, multiplexer_5_out, RSel;

  Multiplexer #(.enable("false"), .select(3)) multiplexer_1 (
    .in0(1'b1), .in1(1'b1), .in2(1'b0), .in3(1'b1), .in4(1'b0), .in5(1'b0), .in6(1'b0), .in7(1'b0),
    .out(RegWEn), .sel(inst[6:4]));
  Multiplexer #(.enable("false"), .select(3), .width(4)) multiplexer_2 (
    .in0(4'b0000), .in1(4'b0110), .in2(4'b0111), .in3(4'b1011), .in4(4'b0011), .in5(4'b0100), .in6(4'b0010),
    .in7(4'b0001), .out(multiplexer_2_out), .sel(inst[14:12]));
  Comparator #(.width(7)) comparator_1 (.a(inst[31:25]), .b(7'b0000001), .eq(comparator_1_eq));  // open: gt, lt
  Comparator #(.width(3)) comparator_2 (.a(inst[14:12]), .b(3'b000), .eq(comparator_2_eq));  // open: gt, lt
  Comparator #(.width(7)) comparator_3 (.a(inst[6:0]), .b(7'b0110011), .eq(comparator_3_eq));  // open: gt, lt
  Comparator #(.width(7)) comparator_4 (.a(inst[31:25]), .b(7'b0000001), .gt(comparator_4_gt));  // open: eq, lt
  Comparator #(.width(3)) comparator_5 (.a(inst[14:12]), .b(3'b000), .eq(comparator_5_eq));  // open: gt, lt
  Comparator #(.width(7)) comparator_6 (.a(inst[6:0]), .b(7'b0110011), .eq(comparator_6_eq));  // open: gt, lt
  Comparator #(.width(7)) comparator_7 (.a(inst[31:25]), .b(7'b0000001), .eq(comparator_7_eq));  // open: gt, lt
  Comparator #(.width(3)) comparator_8 (.a(inst[14:12]), .b(3'b001), .eq(comparator_8_eq));  // open: gt, lt
  Comparator #(.width(7)) comparator_9 (.a(inst[6:0]), .b(7'b0110011), .eq(comparator_9_eq));  // open: gt, lt
  Comparator #(.width(7)) comparator_10 (.a(inst[31:25]), .b(7'b0000001), .gt(comparator_10_gt));  // open: eq, lt
  Comparator #(.width(3)) comparator_11 (.a(inst[14:12]), .b(3'b101), .eq(comparator_11_eq));  // open: gt, lt
  Comparator #(.width(7)) comparator_12 (.a(inst[6:0]), .b(7'b0110011), .eq(comparator_12_eq));  // open: gt, lt
  Comparator #(.width(7)) comparator_13 (.a(inst[6:0]), .b(7'b0010011), .eq(comparator_13_eq));  // open: gt, lt
  Comparator #(.width(7)) comparator_14 (.a(inst[6:0]), .b(7'b0110011), .eq(comparator_14_eq));  // open: gt, lt
  Multiplexer #(.enable("false"), .width(4)) multiplexer_3 (
    .in0(multiplexer_2_out), .in1(4'b1010), .out(multiplexer_3_out), .sel(isMUL));
  and and_1 (isMUL, comparator_1_eq, comparator_2_eq, comparator_3_eq);
  and and_2 (isSUB, comparator_4_gt, comparator_5_eq, comparator_6_eq);
  and and_3 (isMULh, comparator_7_eq, comparator_8_eq, comparator_9_eq);
  and and_4 (isSRA, comparator_10_gt, comparator_11_eq, comparator_12_eq);
  Multiplexer #(.enable("false"), .width(4)) multiplexer_4 (
    .in0(multiplexer_3_out), .in1(4'b1100), .out(multiplexer_4_out), .sel(isSUB));
  or or_1 (or_1_out, comparator_13_eq, comparator_14_eq);
  Multiplexer #(.enable("false"), .width(4)) multiplexer_5 (
    .in0(multiplexer_4_out), .in1(4'b1110), .out(multiplexer_5_out), .sel(isMULh));
  Multiplexer #(.enable("false"), .width(4)) multiplexer_6 (
    .in0(multiplexer_5_out), .in1(4'b0101), .out(RSel), .sel(isSRA));
  Multiplexer #(.enable("false"), .width(4)) multiplexer_7 (.in0(4'b0000), .in1(RSel), .out(ALUSel), .sel(or_1_out));
  Comparator #(.width(7)) comparator_15 (.a(inst[31:25]), .b(7'b0000101), .eq(comparator_15_eq));  // open: gt, lt
  Comparator #(.width(7)) comparator_16 (.a(inst[6:0]), .b(7'b0110011), .eq(is_R_Type));  // open: gt, lt
  Comparator #(.width(7)) comparator_17 (.a(inst[6:0]), .b(7'b0000011), .eq(comparator_17_eq));  // open: gt, lt
  Comparator #(.width(7)) comparator_18 (.a(inst[6:0]), .b(7'b0010011), .eq(comparator_18_eq));  // open: gt, lt
  Comparator #(.width(7)) comparator_19 (.a(inst[6:0]), .b(7'b0010111), .eq(comparator_19_eq));  // open: gt, lt
  Comparator #(.width(7)) comparator_20 (.a(inst[6:0]), .b(7'b0110111), .eq(comparator_20_eq));  // open: gt, lt
  Comparator #(.width(7)) comparator_21 (.a(inst[6:0]), .b(7'b0100011), .eq(MemRW));  // open: gt, lt
  Comparator #(.width(7)) comparator_22 (.a(inst[6:0]), .b(7'b1100011), .eq(is_SB_Type));  // open: gt, lt
  Comparator #(.width(7)) comparator_23 (.a(inst[6:0]), .b(7'b1101111), .eq(is_UJ_Type));  // open: gt, lt
  Comparator #(.width(7)) comparator_24 (.a(inst[6:0]), .b(7'b1100111), .eq(is_JALR_Type));  // open: gt, lt
  Comparator #(.width(7)) comparator_25 (.a(inst[6:0]), .b(7'b1110011), .eq(CSRWen));  // open: gt, lt
  Comparator #(.width(7)) comparator_26 (.a(inst[6:0]), .b(7'b0000011), .eq(is_LOAD_Type));  // open: gt, lt
  Comparator #(.width(3)) comparator_27 (.a(inst[14:12]), .b(3'b000), .eq(comparator_27_eq));  // open: gt, lt
  Comparator #(.width(3)) comparator_28 (.a(inst[14:12]), .b(3'b001), .eq(comparator_28_eq));  // open: gt, lt
  not not_1 (not_1_out, BrEq);
  Comparator #(.width(3)) comparator_29 (.a(inst[14:12]), .b(3'b100), .eq(comparator_29_eq));  // open: gt, lt
  Comparator #(.width(3)) comparator_30 (.a(inst[14:12]), .b(3'b101), .eq(comparator_30_eq));  // open: gt, lt
  not not_2 (not_2_out, BrLt);
  Comparator #(.width(3)) comparator_31 (.a(inst[14:12]), .b(3'b110), .eq(comparator_31_eq));  // open: gt, lt
  Comparator #(.width(3)) comparator_32 (.a(inst[14:12]), .b(3'b111), .eq(comparator_32_eq));  // open: gt, lt
  not not_3 (not_3_out, BrLt);
  or or_2 (is_I_Type, comparator_17_eq, comparator_18_eq);
  or or_3 (is_U_Type, comparator_19_eq, comparator_20_eq);
  and and_5 (is_CSRWI, CSRWen, comparator_15_eq);
  and and_6 (and_6_out, is_SB_Type, comparator_27_eq, BrEq);
  and and_7 (and_7_out, is_SB_Type, comparator_28_eq, not_1_out);
  and and_8 (and_8_out, is_SB_Type, comparator_29_eq, BrLt);
  and and_9 (and_9_out, is_SB_Type, comparator_30_eq, not_2_out);
  and and_10 (and_10_out, is_SB_Type, comparator_31_eq, BrLt);
  and and_11 (and_11_out, is_SB_Type, comparator_32_eq, not_3_out);
  or or_4 (or_4_out, and_6_out, and_7_out, and_8_out, and_9_out, and_10_out, and_11_out);
  Multiplexer #(.enable("false"), .width(3)) multiplexer_8 (
    .in0(3'b000), .in1(3'b001), .out(multiplexer_8_out), .sel(is_I_Type));
  or or_5 (PCSel, or_4_out, is_UJ_Type, is_JALR_Type);
  Multiplexer #(.enable("false"), .width(3)) multiplexer_9 (
    .in0(multiplexer_8_out), .in1(3'b010), .out(multiplexer_9_out), .sel(MemRW));
  Multiplexer #(.enable("false"), .width(3)) multiplexer_10 (
    .in0(multiplexer_9_out), .in1(3'b011), .out(multiplexer_10_out), .sel(is_SB_Type));
  Comparator #(.width(3)) comparator_33 (.a(inst[14:12]), .b(3'b110), .eq(comparator_33_eq));  // open: gt, lt
  Comparator #(.width(3)) comparator_34 (.a(inst[14:12]), .b(3'b111), .eq(comparator_34_eq));  // open: gt, lt
  Comparator #(.width(7)) comparator_35 (.a(inst[6:0]), .b(7'b0010111), .eq(comparator_35_eq));  // open: gt, lt
  Comparator #(.width(7)) comparator_36 (.a(inst[31:25]), .b(7'b0000101), .eq(comparator_36_eq));  // open: gt, lt
  Multiplexer #(.enable("false"), .width(3)) multiplexer_11 (
    .in0(multiplexer_10_out), .in1(3'b100), .out(multiplexer_11_out), .sel(is_U_Type));
  Multiplexer #(.enable("false"), .width(2)) multiplexer_12 (
    .in0(2'b01), .in1(2'b00), .out(multiplexer_12_out), .sel(is_LOAD_Type));
  Multiplexer #(.enable("false"), .width(3)) multiplexer_13 (
    .in0(multiplexer_11_out), .in1(3'b101), .out(multiplexer_13_out), .sel(is_UJ_Type));
  or or_6 (or_6_out, comparator_33_eq, comparator_34_eq);
  and and_12 (and_12_out, CSRWen, comparator_36_eq);
  Multiplexer #(.enable("false"), .width(3)) multiplexer_14 (
    .in0(multiplexer_13_out), .in1(3'b110), .out(ImmSel), .sel(is_CSRWI));
  and and_13 (BrUn, is_SB_Type, or_6_out);
  or or_7 (ASel, is_SB_Type, comparator_35_eq, is_UJ_Type);
  or or_8 (BSel, is_I_Type, is_U_Type, is_UJ_Type, is_JALR_Type, is_SB_Type);
  Multiplexer #(.enable("false"), .width(2)) multiplexer_15 (
    .in0(multiplexer_12_out), .in1(2'b10), .out(WBSel), .sel(or_9_out));
  or or_9 (or_9_out, is_UJ_Type, is_JALR_Type);
  Multiplexer #(.enable("false")) multiplexer_16 (.in0(1'b0), .in1(1'b1), .out(CSRSel), .sel(and_12_out));

  // Other names for the same wires on the sheet: opcode[6:0] = inst[6:0]; opcode_0[3:0] = inst[3:0];
  //   opcode_4[2:0] = inst[6:4]; rd[4:0] = inst[11:7]; funct3[2:0] = inst[14:12]; rs1[4:0] = inst[19:15];
  //   rs2[4:0] = inst[24:20]; funct7[6:0] = inst[31:25]; is_CSR_Type = CSRWen; is_S_Type = MemRW

  // Notes on the sheet:
  //   INPUTS to your circuit
  //   DON'T CHANGE THE LOCATIONS OF THE INPUTS AND OUTPUTS!
  //   OUTPUT from your circuit
  //   ID
endmodule
